// Logisim project PDP-8 CPU Implementation.circ as structural Verilog: 1 circuit, main circuit main
module main (
  output [11:0] out_1,
  output [11:0] out_2,
  output [11:0] out_3,
  output out_4,
  output [11:0] out_5,
  output [2:0] out_6
);

  wire and_1_out, and_2_out, and_3_out, and_4_out, and_5_out, and_6_out, and_7_out, and_8_out, and_9_out,
       and_10_out, clock_1_out, clock_2_out, comparator_1_eq, comparator_2_eq, comparator_3_eq,
       comparator_3_gt, multiplexer_7_out, multiplexer_19_out, multiplexer_20_out, not_1_out, not_2_out,
       not_3_out, not_4_out, not_5_out, not_6_out, not_8_out, not_9_out, or_1_out, or_3_out, register_1_q,
       xor_1_out, xor_2_out, xor_3_out;
  wire [2:0] counter_1_q;
  wire [6:0] MAR_q, multiplexer_8_out;
  wire [10:0] AC_q;
  wire [11:0] adder_1_out, adder_2_out, MBR_q, multiplexer_1_out, multiplexer_3_out, multiplexer_4_out,
       multiplexer_5_out, multiplexer_6_out, multiplexer_9_out, multiplexer_10_out, multiplexer_11_out,
       multiplexer_12_out, multiplexer_13_out, multiplexer_14_out, multiplexer_15_out, multiplexer_16_out,
       multiplexer_17_out, multiplexer_18_out, not_7_out, or_2_out, PC_q, RM_q, shifter_1_out, shifter_2_out;
  wire [11:11] AC_q_2;
  wire [12:0] shifter_3_out, shifter_4_out;
  wire [12:12] Link_Register_q, multiplexer_18_out_2, shifter_1_out_2, shifter_2_out_2;

  not not_1 (not_1_out, AC_q_2[11]);
  not not_2 (not_2_out, comparator_1_eq);
  xor xor_1 (xor_1_out, comparator_1_eq, multiplexer_20_out);
  not not_3 (not_3_out, Link_Register_q[12]);
  or or_1 (or_1_out, AC_q_2[11], comparator_1_eq, Link_Register_q[12]);
  and and_1 (and_1_out, not_1_out, not_2_out, not_3_out);
  Comparator #(.width(12)) comparator_1 (.a({AC_q_2[11], AC_q}), .b({12{1'b0}}), .eq(comparator_1_eq));  // open: gt, lt
  and and_2 (and_2_out, not_2_out, xor_2_out);
  Multiplexer #(.width(12)) multiplexer_1 (
    .in0(PC_q), .in1(adder_2_out), .out(multiplexer_1_out), .sel(xor_1_out));  // open: en
  Multiplexer #(.width(12)) multiplexer_2 (.in0(PC_q), .in1(adder_2_out), .out(out_5), .sel(and_2_out));  // open: en
  xor xor_2 (xor_2_out, AC_q_2[11], multiplexer_20_out);
  Multiplexer #(.width(12)) multiplexer_3 (
    .in0(PC_q), .in1(adder_2_out), .out(multiplexer_3_out), .sel(xor_3_out));  // open: en
  xor xor_3 (xor_3_out, multiplexer_20_out, Link_Register_q[12]);
  and and_3 (and_3_out, and_9_out, or_3_out);
  Comparator #(.width(3)) comparator_2 (.a(3'b100), .b(counter_1_q), .eq(comparator_2_eq));  // open: gt, lt
  Adder #(.width(12)) adder_1 (.a({AC_q_2[11], AC_q}), .b(12'h1), .out(adder_1_out), .cout(out_4));  // open: cin
  Multiplexer #(.width(12)) multiplexer_4 (
    .in0({AC_q_2[11], AC_q}), .in1({12{1'b0}}), .out(multiplexer_4_out), .sel(multiplexer_20_out));  // open: en
  assign or_2_out = {AC_q_2[11], AC_q} | RM_q;  // OR_Gate or_2, 12 bits wide
  Adder #(.width(12)) adder_2 (.a(PC_q), .b(12'h1), .out(adder_2_out));  // open: cin, cout
  Multiplexer #(.width(12)) multiplexer_5 (
    .in0(PC_q), .in1(adder_2_out), .out(multiplexer_5_out), .sel(or_1_out));  // open: en
  Multiplexer #(.width(12)) multiplexer_6 (
    .in0(PC_q), .in1(adder_2_out), .out(multiplexer_6_out), .sel(and_1_out));  // open: en
  Multiplexer #(.select(3)) multiplexer_7 (
    .in0(Link_Register_q[12]), .in1(1'b0), .in2(Link_Register_q[12]), .in3(not_5_out),
    .in4(shifter_1_out_2[12]), .in5(shifter_2_out_2[12]), .in6(multiplexer_18_out_2[12]),
    .in7(Link_Register_q[12]), .out(multiplexer_7_out), .sel(out_6), .en(and_4_out));
  and and_4 (and_4_out, multiplexer_19_out, not_9_out);
  Multiplexer #(.width(7)) multiplexer_8 (
    .in0(MBR_q[6:0]), .in1(out_1[6:0]), .out(multiplexer_8_out), .sel(and_3_out));  // open: en
  or or_3 (or_3_out, comparator_3_eq, comparator_3_gt);
  not not_4 (not_4_out, comparator_2_eq);
  Multiplexer #(.select(3), .width(12)) multiplexer_9 (
    .in0({12{1'b0}}), .in1({AC_q_2[11], AC_q}), .in2(not_7_out), .in3({AC_q_2[11], AC_q}),
    .in4(shifter_1_out), .in5(shifter_2_out), .in6(multiplexer_18_out), .in7(adder_1_out),
    .out(multiplexer_9_out), .sel(out_6), .en(and_5_out));
  and and_5 (and_5_out, multiplexer_19_out, not_9_out);
  Multiplexer #(.select(3), .width(12)) multiplexer_10 (
    .in0(multiplexer_4_out), .in1({AC_q_2[11], AC_q}), .in2({AC_q_2[11], AC_q}), .in3({AC_q_2[11], AC_q}),
    .in4({AC_q_2[11], AC_q}), .in5(or_2_out), .in6({AC_q_2[11], AC_q}), .in7({AC_q_2[11], AC_q}),
    .out(multiplexer_10_out), .sel(out_6));  // open: en
  Multiplexer #(.width(12)) multiplexer_11 (
    .in0(multiplexer_5_out), .in1(multiplexer_6_out), .out(multiplexer_11_out), .sel(MBR_q[3]));  // open: en
  Register #(.width(1)) Link_Register (
    .D(multiplexer_7_out), .Q(Link_Register_q[12]), .clk(multiplexer_20_out));  // open: en, clr
  Comparator #(.width(3)) comparator_3 (
    .a(3'b001), .b(counter_1_q), .gt(comparator_3_gt), .eq(comparator_3_eq));  // open: lt
  Multiplexer #(.select(2), .width(12)) multiplexer_12 (
    .in0(out_1), .in1({{5{1'b0}}, MBR_q[6:0]}), .in2(RM_q), .in3(out_1), .out(multiplexer_12_out),
    .sel(MBR_q[8:7]), .en(not_4_out));
  Multiplexer #(.select(3), .width(12)) multiplexer_13 (
    .in0(PC_q), .in1(out_5), .in2(multiplexer_1_out), .in3(multiplexer_3_out), .in4(multiplexer_11_out),
    .in5(PC_q), .in6(PC_q), .in7(PC_q), .out(multiplexer_13_out), .sel(out_6), .en(and_8_out));
  not not_5 (not_5_out, Link_Register_q[12]);
  Multiplexer #(.select(2), .width(12)) multiplexer_14 (
    .in0({AC_q_2[11], AC_q}), .in1({AC_q_2[11], AC_q}), .in2({AC_q_2[11], AC_q}), .in3(out_3),
    .out(multiplexer_14_out), .sel(counter_1_q[1:0]), .en(not_4_out));
  Multiplexer #(.width(12)) multiplexer_15 (
    .in0(multiplexer_9_out), .in1(multiplexer_10_out), .out(multiplexer_15_out), .sel(and_8_out));  // open: en
  Shifter #(.width(13), .shift("rr")) shifter_1 (
    .in({Link_Register_q[12], AC_q_2[11], AC_q}), .\dist (4'b0001), .out({shifter_1_out_2[12], shifter_1_out}));
  Shifter #(.width(13), .shift("rl")) shifter_2 (
    .in({Link_Register_q[12], AC_q_2[11], AC_q}), .\dist (4'b0001), .out({shifter_2_out_2[12], shifter_2_out}));
  Shifter #(.width(13), .shift("rr")) shifter_3 (
    .in({Link_Register_q[12], AC_q_2[11], AC_q}), .\dist (4'b0010), .out(shifter_3_out));
  not not_6 (not_6_out, and_10_out);
  Multiplexer #(.width(12)) multiplexer_16 (
    .in0(multiplexer_14_out), .in1(multiplexer_15_out), .out(multiplexer_16_out), .sel(and_10_out));  // open: en
  Multiplexer #(.width(12)) multiplexer_17 (
    .in0(multiplexer_12_out), .in1(multiplexer_13_out), .out(multiplexer_17_out), .sel(and_10_out));  // open: en
  assign not_7_out = ~{AC_q_2[11], AC_q};  // NOT_Gate not_7, 12 bits wide
  and and_6 (and_6_out, not_4_out, not_6_out);
  Register #(.width(7)) MAR (.D(multiplexer_8_out), .en(and_6_out), .Q(MAR_q), .clk(clock_1_out));  // open: clr
  Register #(.width(12)) AC (.D(multiplexer_16_out), .Q({AC_q_2[11], AC_q}), .clk(clock_1_out));  // open: en, clr
  Register #(.width(12)) PC (.D(multiplexer_17_out), .Q(PC_q), .clk(clock_1_out));  // open: en, clr
  Register #(.width(12)) RM (.Q(RM_q), .clk(clock_1_out));  // open: D, en, clr
  Subtractor #(.width(12)) subtractor_1 (.a({AC_q_2[11], AC_q}), .b(PC_q), .out(out_3));  // open: bin, bout
  Shifter #(.width(13), .shift("rl")) shifter_4 (
    .in({Link_Register_q[12], AC_q_2[11], AC_q}), .\dist (4'b0010), .out(shifter_4_out));
  not not_8 (not_8_out, and_7_out);
  Clock clock_1 (.out(clock_1_out));
  Multiplexer #(.width(13)) multiplexer_18 (
    .in0(shifter_3_out), .in1(shifter_4_out), .out({multiplexer_18_out_2[12], multiplexer_18_out}),
    .sel(MBR_q[1]));  // open: en
  Register #(.width(1)) register_1 (.D(not_8_out), .Q(register_1_q), .clk(clock_1_out));  // open: en, clr
  Counter #(.width(3), .max('h4), .ongoal("stay"), .trigger("falling")) counter_1 (
    .Q(counter_1_q), .clk(clock_1_out));  // open: load, D, count, carry, clr
  and and_7 (and_7_out, and_8_out, MBR_q[1]);
  and and_8 (and_8_out, and_10_out, MBR_q[8]);
  and and_9 (and_9_out, MBR_q[8], MBR_q[7]);
  not not_9 (not_9_out, and_8_out);
  RAM #(.addrWidth(7), .dataWidth(12)) ram_1 (.addr(MAR_q), .data(out_1), .sel(register_1_q));  // open: clk, ld, clr
  Clock clock_2 (.out(clock_2_out));
  and and_10 (and_10_out, MBR_q[11], MBR_q[10], MBR_q[9]);
  Multiplexer #(.select(3)) multiplexer_19 (
    .in0(MBR_q[7]), .in1(MBR_q[6]), .in2(MBR_q[5]), .in3(MBR_q[4]), .in4(MBR_q[3]), .in5(MBR_q[2]),
    .in6(MBR_q[1]), .in7(MBR_q[0]), .out(multiplexer_19_out), .sel(out_6), .en(not_9_out));
  Counter #(.width(3), .max('h7), .ongoal("stay"), .trigger("falling")) counter_2 (
    .Q(out_6), .clk(clock_1_out));  // open: load, D, count, carry, clr
  Multiplexer #(.select(3)) multiplexer_20 (
    .in0(MBR_q[7]), .in1(MBR_q[6]), .in2(MBR_q[5]), .in3(MBR_q[4]), .in4(MBR_q[3]), .in5(MBR_q[2]),
    .in6(MBR_q[1]), .in7(MBR_q[0]), .out(multiplexer_20_out), .sel(out_6), .en(and_8_out));
  Register #(.width(12)) MBR (.D(out_1), .Q(MBR_q), .clk(clock_2_out));  // open: en, clr

  assign out_2 = out_1;

  // Notes on the sheet:
  //   add select
  //   mem/reg
  //   mem/reg
endmodule
